# Fritzing sketch rangkaian esp32 suhu dan kelembapan (saved by Fritzing 0.9.3b)
breadboards: 1

parts:
  U1 = ESP32-38PinWide [part_number=ESP32-38PinWide]
  DHT1 = DHT22 Humidity and Temperature Sensor

nets:
  N1: U1.3.3, DHT1.VDD
  GND: U1.GND, DHT1.GND
  N2: U1.GPIO4, DHT1.DATA

custom parts:
  ESP32-38PinWide: Generic 38-Pin ESP32 with wide format (only access to one side of pins on a breadboard) based on Stephen Lilley's HiLetgo ESP-WROOM-32 ESP32 ESP-32S Development Board.
